# Fritzing sketch MAX7219-788BS (saved by Fritzing 0.9.2b)
breadboards: 1

parts:
  MAX7219 = IC, DIP package, 24 pins [chip_label=IC]
  788BS = IC, DIP package, 16 pins [chip_label=IC]
  C1 = Ceramic Capacitor [capacitance=10µF package="100 mil [THT, multilayer]"]
  C2 = Ceramic Capacitor [capacitance=0.1µF package="100 mil [THT, multilayer]"]
  R1 = Resistor [tolerance=±5% resistance=28k package=THT]

nets:
  MOSI: MAX7219.pin1
  N1: MAX7219.pin2, 788BS.pin13
  N2: MAX7219.pin3, 788BS.pin6
  GND: MAX7219.pin4, MAX7219.pin9, C1.0, C2.0
  N3: MAX7219.pin5, 788BS.pin15
  N4: MAX7219.pin6, 788BS.pin4
  N5: MAX7219.pin7, 788BS.pin10
  N6: MAX7219.pin8, 788BS.pin16
  N7: MAX7219.pin10, 788BS.pin11
  N8: MAX7219.pin11, 788BS.pin3
  SS: MAX7219.pin12
  SCK: MAX7219.pin13
  N9: MAX7219.pin14, 788BS.pin2
  N10: MAX7219.pin15, 788BS.pin14
  N11: MAX7219.pin16, 788BS.pin7
  N12: MAX7219.pin17, 788BS.pin9
  N13: MAX7219.pin18, R1.Pin_1
  5V: MAX7219.pin19, C1.1, C2.1, R1.Pin_0
  N14: MAX7219.pin20, 788BS.pin1
  N15: MAX7219.pin21, 788BS.pin8
  N16: MAX7219.pin22, 788BS.pin5
  N17: MAX7219.pin23, 788BS.pin12

notes:
  MOSI - connect to pin 51 on Arduino
  SCK - connect to pin 52 on Arduino
  SS - connect ot porper Digital Out on Arduino (see LED_Display.fzz)
  Use externa power source for 5V (not from Arduino)
